# Fritzing sketch LaBoite (saved by Fritzing 0.9.3b)
circuit board: 8.46667cm x 5.64444cm
breadboards: 1

parts:
  Composant1 = Arduino Uno (Rev3)
  U1 = DS1307 [package=so08]
  J1 = Basic Servo
  C3 = Electrolytic Capacitor [capacitance=100μF voltage=25V package="0807 [SMD, electrolytic]"]
  C4 = Electrolytic Capacitor [capacitance=100μF voltage=25V package="0807 [SMD, electrolytic]"]
  CONN1 = USB connector [package=THT]
  Composant2 = Bluetooth HC-05 Macho
  Composant4 = 12 NeoPixel Ring [part_number=1643]

nets:
  N1: Composant1.A4/SDA, U1.SDA
  N2: Composant1.A5/SCL, U1.SCL
  N3: Composant1.D0/RX, Composant2.TXD
  N4: Composant1.D1/TX, Composant2.RXD
  N5: Composant1.D3_PWM, J1.pulse
  N6: Composant1.D6_PWM, Composant4.IN
  VCC: Composant1.5V, U1.VCC, J1.vcc, C3.+, C4.+, Composant4.VDD
  GND: Composant1.GND, U1.GND, J1.gnd, C3.-, C4.-, CONN1.GND, CONN1.chassis5, CONN1.chassis6, Composant4.GND
  VIN: Composant1.VIN, CONN1.5V

custom parts:
  12 NeoPixel Ring: 12 ultra bright smart LED NeoPixels are arranged in a circle with 1.5" (37mm) outer diameter. The rings are 'chainable' - connect the output pin of one to the input pin of another. Use only one microcontroller pin to control as many as you can chain together! Each LED is addressable as the driver chip is inside the LED. Each one has ~18mA constant current drive so the color will be very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
